// Logisim project sap1_flat.circ as structural Verilog: 11 circuits, main circuit main
module main (
  input  in_1,
  input  in_2,
  input  in_3
);

  wire and_1_out, and_2_out, and_3_out, and_4_out, and_6_out, and_7_out, and_8_out, and_9_out, and_10_out,
       and_11_out, and_12_out, and_13_out, and_14_out, and_15_out, and_16_out, and_17_out, and_18_out,
       and_21_out, and_22_out, and_23_out, and_24_out, and_25_out, CE_inv, chip_74ls173_2_q1,
       chip_74ls173_2_q2, chip_74ls173_2_q3, chip_74ls173_2_q4, clk_1_out_5, clock_1_out, COUNT, E_a, E_l,
       E_p, E_u, HLT, j_k_ff_1_q, j_k_ff_2_q, j_k_ff_3_q, j_k_ff_4_q, j_k_ff_5_qn, j_k_ff_6_qn, j_k_ff_7_q,
       j_k_ff_7_qn, j_k_ff_8_q, j_k_ff_8_qn, j_k_ff_9_q, j_k_ff_9_qn, j_k_ff_10_q, j_k_ff_10_qn, L_a_inv,
       L_b_inv, L_l, L_m_inv, L_o_inv, not_1_out, not_2_out, not_3_out, not_4_out, not_5_out, not_6_out,
       not_7_out, not_8_out, not_9_out, or_1_out, or_2_out, or_3_out, or_4_out, or_6_out, SUBTRACT;
  wire [3:0] chip_74ls173_1_q4;
  wire [7:0] adder_1_out, bit_extender_1_out, chip_74ls173_6_q1, chip_74ls173_8_q4, chip_74ls173_9_q4,
       controlled_buffer_4_out, ram_1_dout, xor_1_out;

  Clock clock_1 (.out(clock_1_out));
  J_K_Flip_Flop j_k_ff_1 (.J(COUNT), .K(COUNT), .clk(clk_1_out_5), .Q(j_k_ff_1_q), .reset(in_1));  // open: Qn, preset
  assign controlled_buffer_4_out[7] = E_p ? j_k_ff_1_q : 1'bz;  // Controlled_Buffer controlled_buffer_1
  chip_74LS173 chip_74ls173_1 (
    .D1(controlled_buffer_4_out[4]), .D2(controlled_buffer_4_out[5]), .D3(controlled_buffer_4_out[6]),
    .D4(controlled_buffer_4_out[7]), .IE1(L_m_inv), .IE2(L_m_inv), .CLK(clk_1_out_5), .CLR(in_1), .OE1(1'b0),
    .OE2(1'b0), .Q1(chip_74ls173_1_q4[3]), .Q2(chip_74ls173_1_q4[2]), .Q3(chip_74ls173_1_q4[1]),
    .Q4(chip_74ls173_1_q4[0]));
  chip_74LS173 chip_74ls173_2 (
    .D1(controlled_buffer_4_out[0]), .D2(controlled_buffer_4_out[1]), .D3(controlled_buffer_4_out[2]),
    .D4(controlled_buffer_4_out[3]), .IE1(L_l), .IE2(L_l), .CLK(clk_1_out_5), .CLR(in_1), .OE1(1'b0),
    .OE2(1'b0), .Q1(chip_74ls173_2_q1), .Q2(chip_74ls173_2_q2), .Q3(chip_74ls173_2_q3), .Q4(chip_74ls173_2_q4));
  CLK clk_1 (.CLK_IN(clock_1_out), .CLK_E(in_2), .MANUAL_CLK(in_3), .HLT(HLT), .out_5(clk_1_out_5));
  J_K_Flip_Flop j_k_ff_2 (.J(COUNT), .K(COUNT), .clk(not_1_out), .Q(j_k_ff_2_q), .reset(in_1));  // open: Qn, preset
  not not_1 (not_1_out, j_k_ff_1_q);
  RAM #(.addrWidth(4), .trigger("high")) ram_1 (.addr(chip_74ls173_1_q4), .dout(ram_1_dout));  // open: we, oe, din
  not not_2 (not_2_out, chip_74ls173_2_q1);
  not not_3 (not_3_out, chip_74ls173_2_q2);
  not not_4 (not_4_out, chip_74ls173_2_q3);
  not not_5 (not_5_out, chip_74ls173_2_q4);
  and and_1 (and_1_out, not_2_out, not_3_out, not_4_out, not_5_out);
  and and_2 (and_2_out, not_2_out, not_3_out, not_4_out, chip_74ls173_2_q4);
  and and_3 (and_3_out, not_2_out, not_3_out, chip_74ls173_2_q3, not_5_out);
  and and_4 (and_4_out, chip_74ls173_2_q1, chip_74ls173_2_q2, chip_74ls173_2_q3, not_5_out);
  and and_5 (HLT, chip_74ls173_2_q1, chip_74ls173_2_q2, chip_74ls173_2_q3, chip_74ls173_2_q4);
  assign controlled_buffer_4_out[6] = E_p ? j_k_ff_2_q : 1'bz;  // Controlled_Buffer controlled_buffer_2
  J_K_Flip_Flop j_k_ff_3 (.J(COUNT), .K(COUNT), .clk(not_6_out), .Q(j_k_ff_3_q), .reset(in_1));  // open: Qn, preset
  not not_6 (not_6_out, j_k_ff_2_q);
  not not_7 (not_7_out, CE_inv);
  chip_74LS173 chip_74ls173_3 (
    .D1(controlled_buffer_4_out[4]), .D2(controlled_buffer_4_out[5]), .D3(controlled_buffer_4_out[6]),
    .D4(controlled_buffer_4_out[7]), .IE1(L_l), .IE2(L_l), .CLK(clk_1_out_5), .CLR(1'b0), .OE1(E_l),
    .OE2(E_l), .Q1(controlled_buffer_4_out[4]), .Q2(controlled_buffer_4_out[5]),
    .Q3(controlled_buffer_4_out[6]), .Q4(controlled_buffer_4_out[7]));
  not not_8 (not_8_out, clk_1_out_5);
  J_K_Flip_Flop j_k_ff_4 (.J(COUNT), .K(COUNT), .clk(not_9_out), .Q(j_k_ff_4_q), .reset(in_1));  // open: Qn, preset
  not not_9 (not_9_out, j_k_ff_3_q);
  assign controlled_buffer_4_out[5] = E_p ? j_k_ff_3_q : 1'bz;  // Controlled_Buffer controlled_buffer_3
  assign {controlled_buffer_4_out[0], controlled_buffer_4_out[1], controlled_buffer_4_out[2], controlled_buffer_4_out[3], controlled_buffer_4_out[4], controlled_buffer_4_out[5], controlled_buffer_4_out[6], controlled_buffer_4_out[7]} = not_7_out ? ram_1_dout : 8'bz;  // Controlled_Buffer controlled_buffer_4
  and and_6 (and_6_out, ~j_k_ff_10_q, ~j_k_ff_9_q, ~j_k_ff_8_q, ~j_k_ff_7_q, ~COUNT, ~E_p);  // AND_Gate
  J_K_Flip_Flop j_k_ff_5 (
    .J(j_k_ff_10_q), .K(j_k_ff_10_qn), .clk(not_8_out), .Q(E_p), .Qn(j_k_ff_5_qn), .preset(and_6_out));  // open: reset
  and and_7 (and_7_out, and_1_out, j_k_ff_8_q);
  assign controlled_buffer_4_out[4] = E_p ? j_k_ff_4_q : 1'bz;  // Controlled_Buffer controlled_buffer_5
  J_K_Flip_Flop j_k_ff_6 (
    .J(E_p), .K(j_k_ff_5_qn), .clk(not_8_out), .Q(COUNT), .Qn(j_k_ff_6_qn), .reset(in_1));  // open: preset
  and and_8 (and_8_out, and_2_out, j_k_ff_8_q);
  and and_9 (and_9_out, and_3_out, j_k_ff_8_q);
  or or_1 (or_1_out, E_p, and_7_out, and_8_out, and_9_out);
  not not_10 (L_m_inv, or_1_out);
  LED led_1 (.in(controlled_buffer_4_out[0]));
  LED led_2 (.in(controlled_buffer_4_out[1]));
  LED led_3 (.in(controlled_buffer_4_out[2]));
  LED led_4 (.in(controlled_buffer_4_out[3]));
  J_K_Flip_Flop j_k_ff_7 (
    .J(COUNT), .K(j_k_ff_6_qn), .clk(not_8_out), .Q(j_k_ff_7_q), .Qn(j_k_ff_7_qn), .reset(in_1));  // open: preset
  and and_10 (and_10_out, and_1_out, j_k_ff_9_q);
  and and_11 (and_11_out, and_2_out, j_k_ff_9_q);
  or or_2 (or_2_out, j_k_ff_7_q, and_10_out, and_11_out, and_12_out);
  not not_11 (CE_inv, or_2_out);
  LED led_5 (.in(controlled_buffer_4_out[6]));
  LED led_6 (.in(controlled_buffer_4_out[7]));
  LED led_7 (.in(controlled_buffer_4_out[4]));
  LED led_8 (.in(controlled_buffer_4_out[5]));
  J_K_Flip_Flop j_k_ff_8 (
    .J(j_k_ff_7_q), .K(j_k_ff_7_qn), .clk(not_8_out), .Q(j_k_ff_8_q), .Qn(j_k_ff_8_qn), .reset(in_1));  // open: preset
  and and_12 (and_12_out, and_3_out, j_k_ff_9_q);
  assign controlled_buffer_4_out[7] = E_a ? chip_74ls173_8_q4[0] : 1'bz;  // Controlled_Buffer controlled_buffer_6
  assign controlled_buffer_4_out[6] = E_a ? chip_74ls173_8_q4[1] : 1'bz;  // Controlled_Buffer controlled_buffer_7
  assign controlled_buffer_4_out[5] = E_a ? chip_74ls173_8_q4[2] : 1'bz;  // Controlled_Buffer controlled_buffer_8
  assign controlled_buffer_4_out[4] = E_a ? chip_74ls173_8_q4[3] : 1'bz;  // Controlled_Buffer controlled_buffer_9
  assign controlled_buffer_4_out[3] = E_a ? chip_74ls173_8_q4[4] : 1'bz;  // Controlled_Buffer controlled_buffer_10
  assign controlled_buffer_4_out[2] = E_a ? chip_74ls173_8_q4[5] : 1'bz;  // Controlled_Buffer controlled_buffer_11
  assign controlled_buffer_4_out[1] = E_a ? chip_74ls173_8_q4[6] : 1'bz;  // Controlled_Buffer controlled_buffer_12
  assign controlled_buffer_4_out[0] = E_a ? chip_74ls173_8_q4[7] : 1'bz;  // Controlled_Buffer controlled_buffer_13
  J_K_Flip_Flop j_k_ff_9 (
    .J(j_k_ff_8_q), .K(j_k_ff_8_qn), .clk(not_8_out), .Q(j_k_ff_9_q), .Qn(j_k_ff_9_qn), .reset(in_1));  // open: preset
  and and_13 (and_13_out, and_1_out, j_k_ff_8_q);
  not not_12 (L_l, j_k_ff_7_q);
  J_K_Flip_Flop j_k_ff_10 (
    .J(j_k_ff_9_q), .K(j_k_ff_9_qn), .clk(not_8_out), .Q(j_k_ff_10_q), .Qn(j_k_ff_10_qn), .reset(in_1));  // open: preset
  and and_14 (and_14_out, and_2_out, j_k_ff_8_q);
  or or_3 (or_3_out, and_13_out, and_14_out, and_15_out);
  not not_13 (E_l, or_3_out);
  chip_74LS173 chip_74ls173_4 (
    .D1(controlled_buffer_4_out[3]), .D2(controlled_buffer_4_out[2]), .D3(controlled_buffer_4_out[1]),
    .D4(controlled_buffer_4_out[0]), .IE1(L_b_inv), .IE2(L_b_inv), .CLK(clk_1_out_5), .CLR(1'b0), .OE1(1'b0),
    .OE2(1'b0), .Q1(chip_74ls173_6_q1[4]), .Q2(chip_74ls173_6_q1[5]), .Q3(chip_74ls173_6_q1[6]),
    .Q4(chip_74ls173_6_q1[7]));
  and and_15 (and_15_out, and_3_out, j_k_ff_8_q);
  and and_16 (and_16_out, and_1_out, j_k_ff_9_q);
  chip_74LS173 chip_74ls173_5 (
    .D1(controlled_buffer_4_out[0]), .D2(controlled_buffer_4_out[1]), .D3(controlled_buffer_4_out[2]),
    .D4(controlled_buffer_4_out[3]), .IE1(L_a_inv), .IE2(L_a_inv), .CLK(clk_1_out_5), .CLR(1'b0), .OE1(1'b0),
    .OE2(1'b0), .Q1(chip_74ls173_8_q4[7]), .Q2(chip_74ls173_8_q4[6]), .Q3(chip_74ls173_8_q4[5]),
    .Q4(chip_74ls173_8_q4[4]));
  assign bit_extender_1_out = {{7{SUBTRACT}}, SUBTRACT};  // Bit_Extender bit_extender_1
  chip_74LS173 chip_74ls173_6 (
    .D1(controlled_buffer_4_out[7]), .D2(controlled_buffer_4_out[6]), .D3(controlled_buffer_4_out[5]),
    .D4(controlled_buffer_4_out[4]), .IE1(L_b_inv), .IE2(L_b_inv), .CLK(clk_1_out_5), .CLR(1'b0), .OE1(1'b0),
    .OE2(1'b0), .Q1(chip_74ls173_6_q1[0]), .Q2(chip_74ls173_6_q1[1]), .Q3(chip_74ls173_6_q1[2]),
    .Q4(chip_74ls173_6_q1[3]));
  chip_74LS173 chip_74ls173_7 (
    .D1(controlled_buffer_4_out[7]), .D2(controlled_buffer_4_out[6]), .D3(controlled_buffer_4_out[5]),
    .D4(controlled_buffer_4_out[4]), .IE1(L_o_inv), .IE2(L_o_inv), .CLK(clk_1_out_5), .CLR(1'b0), .OE1(1'b0),
    .OE2(1'b0), .Q1(chip_74ls173_9_q4[7]), .Q2(chip_74ls173_9_q4[6]), .Q3(chip_74ls173_9_q4[5]),
    .Q4(chip_74ls173_9_q4[4]));
  and and_17 (and_17_out, and_2_out, j_k_ff_10_q);
  or or_4 (or_4_out, and_16_out, and_17_out, and_18_out);
  not not_14 (L_a_inv, or_4_out);
  assign xor_1_out = bit_extender_1_out ^ chip_74ls173_6_q1;  // XOR_Gate xor_1, 8 bits wide
  and and_18 (and_18_out, and_3_out, j_k_ff_10_q);
  chip_74LS173 chip_74ls173_8 (
    .D1(controlled_buffer_4_out[4]), .D2(controlled_buffer_4_out[5]), .D3(controlled_buffer_4_out[6]),
    .D4(controlled_buffer_4_out[7]), .IE1(L_a_inv), .IE2(L_a_inv), .CLK(clk_1_out_5), .CLR(1'b0), .OE1(1'b0),
    .OE2(1'b0), .Q1(chip_74ls173_8_q4[3]), .Q2(chip_74ls173_8_q4[2]), .Q3(chip_74ls173_8_q4[1]),
    .Q4(chip_74ls173_8_q4[0]));
  Adder adder_1 (.a(chip_74ls173_8_q4), .b(xor_1_out), .out(adder_1_out), .cin(SUBTRACT));  // open: cout
  chip_74LS173 chip_74ls173_9 (
    .D1(controlled_buffer_4_out[3]), .D2(controlled_buffer_4_out[2]), .D3(controlled_buffer_4_out[1]),
    .D4(controlled_buffer_4_out[0]), .IE1(L_o_inv), .IE2(L_o_inv), .CLK(clk_1_out_5), .CLR(1'b0), .OE1(1'b0),
    .OE2(1'b0), .Q1(chip_74ls173_9_q4[3]), .Q2(chip_74ls173_9_q4[2]), .Q3(chip_74ls173_9_q4[1]),
    .Q4(chip_74ls173_9_q4[0]));
  and and_19 (E_a, and_4_out, j_k_ff_8_q);
  assign controlled_buffer_4_out = E_u ? adder_1_out : 8'bz;  // Controlled_Buffer controlled_buffer_14
  // BCD_to_7_Segment_decoder bcd_to_7_segment_decoder_1: pin names not known
  _7_Segment_Display u_7_segment_display_1 ();  // open: g, f, a, b, e, d, c, dp
  // Binary_to_BCD_converter #(.binvalue(8)) binary_to_bcd_converter_1: pin names not known; wires that end beside it: chip_74ls173_9_q4
  and and_20 (SUBTRACT, and_3_out, j_k_ff_10_q);
  // BCD_to_7_Segment_decoder bcd_to_7_segment_decoder_2: pin names not known
  _7_Segment_Display u_7_segment_display_2 ();  // open: g, f, a, b, e, d, c, dp
  and and_21 (and_21_out, and_2_out, j_k_ff_10_q);
  or or_5 (E_u, and_21_out, and_22_out);
  // BCD_to_7_Segment_decoder bcd_to_7_segment_decoder_3: pin names not known
  _7_Segment_Display u_7_segment_display_3 ();  // open: g, f, a, b, e, d, c, dp
  and and_22 (and_22_out, and_3_out, j_k_ff_10_q);
  and and_23 (and_23_out, and_2_out, j_k_ff_9_q);
  and and_24 (and_24_out, and_3_out, j_k_ff_9_q);
  or or_6 (or_6_out, and_23_out, and_24_out);
  not not_15 (L_b_inv, or_6_out);
  and and_25 (and_25_out, and_4_out, j_k_ff_8_q);
  not not_16 (L_o_inv, and_25_out);

  // Other names for the same wires on the sheet: CLR = in_1

  // Notes on the sheet:
  //   LDA
  //   ADD
  //   SUB
  //   OUT
  //   HLT
endmodule

module chip_74LS173 (
  input  D1,
  input  D2,
  input  D3,
  input  D4,
  input  IE1,
  input  IE2,
  input  CLK,
  input  CLR,
  input  OE1,
  input  OE2,
  output Q1,
  output Q2,
  output Q3,
  output Q4
);

  wire and_1_out, and_2_out, and_3_out, and_4_out, and_5_out, and_6_out, and_7_out, and_8_out, and_9_out,
       and_10_out, d_ff_1_q, d_ff_2_q, d_ff_3_q, d_ff_4_q, not_1_out, or_1_out, or_2_out, or_3_out, or_4_out;

  and and_1 (and_1_out, ~IE1, ~IE2);  // AND_Gate
  and and_2 (and_2_out, ~OE1, ~OE2);  // AND_Gate
  and and_3 (and_3_out, and_1_out, D1);
  not not_1 (not_1_out, and_1_out);
  and and_4 (and_4_out, not_1_out, d_ff_1_q);
  or or_1 (or_1_out, and_3_out, and_4_out);
  D_Flip_Flop d_ff_1 (.D(or_1_out), .clk(CLK), .Q(d_ff_1_q), .reset(CLR));  // open: Qn, preset
  and and_5 (and_5_out, and_1_out, D2);
  and and_6 (and_6_out, not_1_out, d_ff_2_q);
  or or_2 (or_2_out, and_5_out, and_6_out);
  D_Flip_Flop d_ff_2 (.D(or_2_out), .clk(CLK), .Q(d_ff_2_q), .reset(CLR));  // open: Qn, preset
  and and_7 (and_7_out, and_1_out, D3);
  and and_8 (and_8_out, not_1_out, d_ff_3_q);
  or or_3 (or_3_out, and_7_out, and_8_out);
  D_Flip_Flop d_ff_3 (.D(or_3_out), .clk(CLK), .Q(d_ff_3_q), .reset(CLR));  // open: Qn, preset
  and and_9 (and_9_out, and_1_out, D4);
  or or_4 (or_4_out, and_9_out, and_10_out);
  D_Flip_Flop d_ff_4 (.D(or_4_out), .clk(CLK), .Q(d_ff_4_q), .reset(CLR));  // open: Qn, preset
  and and_10 (and_10_out, not_1_out, d_ff_4_q);
  assign Q1 = and_2_out ? d_ff_1_q : 1'bz;  // Controlled_Buffer controlled_buffer_1
  assign Q2 = and_2_out ? d_ff_2_q : 1'bz;  // Controlled_Buffer controlled_buffer_2
  assign Q3 = and_2_out ? d_ff_3_q : 1'bz;  // Controlled_Buffer controlled_buffer_3
  assign Q4 = and_2_out ? d_ff_4_q : 1'bz;  // Controlled_Buffer controlled_buffer_4
endmodule

module register_b (
  input  [7:0] I,
  input  IE_inv,
  input  CLK,
  output [7:0] O
);

  chip_74LS173 chip_74ls173_1 (
    .D1(I[7]), .D2(I[6]), .D3(I[5]), .D4(I[4]), .IE1(IE_inv), .IE2(IE_inv), .CLK(CLK), .CLR(1'b0),
    .OE1(1'b0), .OE2(1'b0), .Q1(O[7]), .Q2(O[6]), .Q3(O[5]), .Q4(O[4]));
  chip_74LS173 chip_74ls173_2 (
    .D1(I[3]), .D2(I[2]), .D3(I[1]), .D4(I[0]), .IE1(IE_inv), .IE2(IE_inv), .CLK(CLK), .CLR(1'b0),
    .OE1(1'b0), .OE2(1'b0), .Q1(O[3]), .Q2(O[2]), .Q3(O[1]), .Q4(O[0]));
endmodule

module program_counter (
  input  C,
  input  CLK,
  input  CLR_inv,
  input  E,
  output Q1,
  output Q2,
  output Q3,
  output Q4
);

  wire j_k_ff_1_q, j_k_ff_2_q, j_k_ff_3_q, j_k_ff_4_q, not_1_out, not_2_out, not_3_out;

  J_K_Flip_Flop j_k_ff_1 (.J(C), .K(C), .clk(CLK), .Q(j_k_ff_1_q), .reset(CLR_inv));  // open: Qn, preset
  not not_1 (not_1_out, j_k_ff_1_q);
  assign Q4 = E ? j_k_ff_1_q : 1'bz;  // Controlled_Buffer controlled_buffer_1
  J_K_Flip_Flop j_k_ff_2 (.J(C), .K(C), .clk(not_1_out), .Q(j_k_ff_2_q), .reset(CLR_inv));  // open: Qn, preset
  assign Q3 = E ? j_k_ff_2_q : 1'bz;  // Controlled_Buffer controlled_buffer_2
  J_K_Flip_Flop j_k_ff_3 (.J(C), .K(C), .clk(not_2_out), .Q(j_k_ff_3_q), .reset(CLR_inv));  // open: Qn, preset
  not not_2 (not_2_out, j_k_ff_2_q);
  assign Q2 = E ? j_k_ff_3_q : 1'bz;  // Controlled_Buffer controlled_buffer_3
  J_K_Flip_Flop j_k_ff_4 (.J(C), .K(C), .clk(not_3_out), .Q(j_k_ff_4_q), .reset(CLR_inv));  // open: Qn, preset
  not not_3 (not_3_out, j_k_ff_3_q);
  assign Q1 = E ? j_k_ff_4_q : 1'bz;  // Controlled_Buffer controlled_buffer_4
endmodule

module register_a (
  input  [7:0] I,
  input  LE_inv,
  input  CLK,
  input  OE,
  output [7:0] out_5,
  output [7:0] ALWAYS_OUT
);

  chip_74LS173 chip_74ls173_1 (
    .D1(I[7]), .D2(I[6]), .D3(I[5]), .D4(I[4]), .IE1(LE_inv), .IE2(LE_inv), .CLK(CLK), .CLR(1'b0),
    .OE1(1'b0), .OE2(1'b0), .Q1(ALWAYS_OUT[7]), .Q2(ALWAYS_OUT[6]), .Q3(ALWAYS_OUT[5]), .Q4(ALWAYS_OUT[4]));
  chip_74LS173 chip_74ls173_2 (
    .D1(I[3]), .D2(I[2]), .D3(I[1]), .D4(I[0]), .IE1(LE_inv), .IE2(LE_inv), .CLK(CLK), .CLR(1'b0),
    .OE1(1'b0), .OE2(1'b0), .Q1(ALWAYS_OUT[3]), .Q2(ALWAYS_OUT[2]), .Q3(ALWAYS_OUT[1]), .Q4(ALWAYS_OUT[0]));
  assign out_5 = OE ? ALWAYS_OUT : 8'bz;  // Controlled_Buffer controlled_buffer_1
endmodule

module ALU (
  input  [7:0] register_a,
  input  [7:0] register_b,
  input  S,
  input  EO,
  output [7:0] out_5
);

  wire [7:0] adder_1_out, bit_extender_1_out, xor_1_out;

  assign bit_extender_1_out = {{7{S}}, S};  // Bit_Extender bit_extender_1
  assign xor_1_out = register_b ^ bit_extender_1_out;  // XOR_Gate xor_1, 8 bits wide
  Adder adder_1 (.a(register_a), .b(xor_1_out), .out(adder_1_out), .cin(S));  // open: cout
  assign out_5 = EO ? adder_1_out : 8'bz;  // Controlled_Buffer controlled_buffer_1
endmodule

module instruction_register (
  input  [7:0] I,
  input  LE_inv,
  input  CLK,
  input  CLR,
  input  OE,
  output [3:0] out_6,
  output [3:0] out_7
);

  wire [3:0] chip_74ls173_1_q4;

  chip_74LS173 chip_74ls173_1 (
    .D1(I[7]), .D2(I[6]), .D3(I[5]), .D4(I[4]), .IE1(LE_inv), .IE2(LE_inv), .CLK(CLK), .CLR(1'b0),
    .OE1(1'b0), .OE2(1'b0), .Q1(chip_74ls173_1_q4[3]), .Q2(chip_74ls173_1_q4[2]), .Q3(chip_74ls173_1_q4[1]),
    .Q4(chip_74ls173_1_q4[0]));
  chip_74LS173 chip_74ls173_2 (
    .D1(I[3]), .D2(I[2]), .D3(I[1]), .D4(I[0]), .IE1(LE_inv), .IE2(LE_inv), .CLK(CLK), .CLR(CLR), .OE1(1'b0),
    .OE2(1'b0), .Q1(out_6[3]), .Q2(out_6[2]), .Q3(out_6[1]), .Q4(out_6[0]));
  assign out_7 = OE ? chip_74ls173_1_q4 : 4'bz;  // Controlled_Buffer controlled_buffer_1
endmodule

module MAR (
  input  [3:0] in_1,
  input  LE_inv,
  input  CLK,
  input  CLR,
  output [3:0] out_5
);

  chip_74LS173 chip_74ls173_1 (
    .D1(in_1[3]), .D2(in_1[2]), .D3(in_1[1]), .D4(in_1[0]), .IE1(LE_inv), .IE2(LE_inv), .CLK(CLK), .CLR(CLR),
    .Q1(out_5[3]), .Q2(out_5[2]), .Q3(out_5[1]), .Q4(out_5[0]));  // open: OE1, OE2
endmodule

module controller (
  input  CLK,
  input  CLR,
  input  I1,
  input  I2,
  input  I3,
  input  I4,
  output HLT,
  output E_p,
  output L_m_inv,
  output CE_inv,
  output L_l,
  output E_l_inv,
  output L_a_inv,
  output E_a,
  output S_u,
  output E_u,
  output L_b_inv,
  output L_o_inv,
  output C_p
);

  wire and_1_out, and_2_out, and_3_out, and_4_out, and_6_out, and_7_out, and_8_out, and_9_out, and_10_out,
       and_11_out, and_12_out, and_13_out, and_14_out, and_15_out, and_16_out, and_17_out, and_18_out,
       and_21_out, and_22_out, and_23_out, and_24_out, and_25_out, j_k_ff_1_qn, j_k_ff_2_qn, j_k_ff_3_q,
       j_k_ff_3_qn, j_k_ff_4_q, j_k_ff_4_qn, j_k_ff_5_q, j_k_ff_5_qn, j_k_ff_6_q, j_k_ff_6_qn, not_1_out,
       not_2_out, not_3_out, not_4_out, not_5_out, or_1_out, or_2_out, or_3_out, or_4_out, or_6_out;

  not not_1 (not_1_out, I1);
  not not_2 (not_2_out, I2);
  not not_3 (not_3_out, I3);
  not not_4 (not_4_out, I4);
  and and_1 (and_1_out, not_1_out, not_2_out, not_3_out, not_4_out);
  and and_2 (and_2_out, not_1_out, not_2_out, not_3_out, I4);
  and and_3 (and_3_out, not_1_out, not_2_out, I3, not_4_out);
  and and_4 (and_4_out, I1, I2, I3, not_4_out);
  and and_5 (HLT, I1, I2, I3, I4);
  not not_5 (not_5_out, CLK);
  and and_6 (and_6_out, and_1_out, j_k_ff_4_q);
  and and_7 (and_7_out, ~j_k_ff_6_q, ~j_k_ff_5_q, ~j_k_ff_4_q, ~j_k_ff_3_q, ~C_p, ~E_p);  // AND_Gate
  J_K_Flip_Flop j_k_ff_1 (
    .J(j_k_ff_6_q), .K(j_k_ff_6_qn), .clk(not_5_out), .Q(E_p), .Qn(j_k_ff_1_qn), .preset(and_7_out));  // open: reset
  and and_8 (and_8_out, and_2_out, j_k_ff_4_q);
  or or_1 (or_1_out, E_p, and_6_out, and_8_out, and_9_out);
  not not_6 (L_m_inv, or_1_out);
  J_K_Flip_Flop j_k_ff_2 (
    .J(E_p), .K(j_k_ff_1_qn), .clk(not_5_out), .Q(C_p), .Qn(j_k_ff_2_qn), .reset(CLR));  // open: preset
  and and_9 (and_9_out, and_3_out, j_k_ff_4_q);
  J_K_Flip_Flop j_k_ff_3 (
    .J(C_p), .K(j_k_ff_2_qn), .clk(not_5_out), .Q(j_k_ff_3_q), .Qn(j_k_ff_3_qn), .reset(CLR));  // open: preset
  and and_10 (and_10_out, and_1_out, j_k_ff_5_q);
  J_K_Flip_Flop j_k_ff_4 (
    .J(j_k_ff_3_q), .K(j_k_ff_3_qn), .clk(not_5_out), .Q(j_k_ff_4_q), .Qn(j_k_ff_4_qn), .reset(CLR));  // open: preset
  and and_11 (and_11_out, and_2_out, j_k_ff_5_q);
  or or_2 (or_2_out, j_k_ff_3_q, and_10_out, and_11_out, and_12_out);
  not not_7 (CE_inv, or_2_out);
  J_K_Flip_Flop j_k_ff_5 (
    .J(j_k_ff_4_q), .K(j_k_ff_4_qn), .clk(not_5_out), .Q(j_k_ff_5_q), .Qn(j_k_ff_5_qn), .reset(CLR));  // open: preset
  and and_12 (and_12_out, and_3_out, j_k_ff_5_q);
  not not_8 (L_l, j_k_ff_3_q);
  J_K_Flip_Flop j_k_ff_6 (
    .J(j_k_ff_5_q), .K(j_k_ff_5_qn), .clk(not_5_out), .Q(j_k_ff_6_q), .Qn(j_k_ff_6_qn), .reset(CLR));  // open: preset
  and and_13 (and_13_out, and_1_out, j_k_ff_4_q);
  and and_14 (and_14_out, and_3_out, j_k_ff_4_q);
  and and_15 (and_15_out, and_2_out, j_k_ff_4_q);
  or or_3 (or_3_out, and_13_out, and_15_out, and_14_out);
  not not_9 (E_l_inv, or_3_out);
  and and_16 (and_16_out, and_1_out, j_k_ff_5_q);
  and and_17 (and_17_out, and_2_out, j_k_ff_6_q);
  or or_4 (or_4_out, and_16_out, and_17_out, and_18_out);
  not not_10 (L_a_inv, or_4_out);
  and and_18 (and_18_out, and_3_out, j_k_ff_6_q);
  and and_19 (E_a, and_4_out, j_k_ff_4_q);
  and and_20 (S_u, and_3_out, j_k_ff_6_q);
  and and_21 (and_21_out, and_2_out, j_k_ff_6_q);
  and and_22 (and_22_out, and_3_out, j_k_ff_6_q);
  or or_5 (E_u, and_21_out, and_22_out);
  and and_23 (and_23_out, and_2_out, j_k_ff_5_q);
  or or_6 (or_6_out, and_23_out, and_24_out);
  not not_11 (L_b_inv, or_6_out);
  and and_24 (and_24_out, and_3_out, j_k_ff_5_q);
  and and_25 (and_25_out, and_4_out, j_k_ff_4_q);
  not not_12 (L_o_inv, and_25_out);

  // Notes on the sheet:
  //   LDA
  //   ADD
  //   SUB
  //   OUT
  //   HLT
endmodule

module CLK (
  input  CLK_IN,
  input  CLK_E,
  input  MANUAL_CLK,
  input  HLT,
  output out_5
);

  wire and_1_out, and_2_out, not_1_out, not_2_out, or_1_out;

  not not_1 (not_1_out, CLK_E);
  not not_2 (not_2_out, HLT);
  and and_1 (and_1_out, CLK_IN, CLK_E);
  and and_2 (and_2_out, not_1_out, MANUAL_CLK);
  or or_1 (or_1_out, and_1_out, and_2_out);
  and and_3 (out_5, or_1_out, not_2_out);
endmodule

module ouput_register (
  input  [7:0] I,
  input  WE,
  input  CLK,
  input  CLR,
  output [7:0] O
);

  Register register_1 (.D(I), .en(WE), .clk(CLK), .Q(O), .clr(CLR));
endmodule
